// Logisim project Verrou.circ as structural Verilog
module Verrou (
  input  h,
  input  e,
  output S
);

  wire and_1_out, and_2_out, not_1_out, not_2_out, not_3_out, or_1_out;

  not not_1 (not_1_out, e);
  and and_1 (and_1_out, h, not_1_out);
  and and_2 (and_2_out, h, e);
  or or_1 (or_1_out, and_1_out, not_2_out);
  not not_2 (not_2_out, S);
  not not_3 (not_3_out, or_1_out);
  or or_2 (S, not_3_out, and_2_out);
endmodule

module Verrou_clock (
  input  e,
  output S
);

  wire and_1_out, and_2_out, clock_1_out, not_1_out, not_2_out, not_3_out, or_1_out;

  not not_1 (not_1_out, e);
  Clock clock_1 (.out(clock_1_out));
  and and_1 (and_1_out, clock_1_out, not_1_out);
  and and_2 (and_2_out, clock_1_out, e);
  or or_1 (or_1_out, and_1_out, not_2_out);
  not not_2 (not_2_out, S);
  not not_3 (not_3_out, or_1_out);
  or or_2 (S, not_3_out, and_2_out);
endmodule

// BD
module Bacule_D (
  input  h,
  input  e,
  output S
);

  wire not_1_out, verrou_1_s;

  Verrou verrou_1 (.e(e), .h(h), .S(verrou_1_s));
  not not_1 (not_1_out, h);
  Verrou verrou_2 (.e(verrou_1_s), .h(not_1_out), .S(S));
endmodule

module Retardateur (
  input  in_1,
  output S
);

  wire clock_1_out, not_1_out, not_2_out, not_3_out, verrou_1_s, verrou_2_s, verrou_3_s, verrou_4_s,
       verrou_5_s;

  Clock clock_1 (.out(clock_1_out));
  Verrou verrou_1 (.e(in_1), .h(clock_1_out), .S(verrou_1_s));
  not not_1 (not_1_out, clock_1_out);
  Verrou verrou_2 (.e(verrou_1_s), .h(not_1_out), .S(verrou_2_s));
  Verrou verrou_3 (.e(verrou_2_s), .h(clock_1_out), .S(verrou_3_s));
  not not_2 (not_2_out, clock_1_out);
  Verrou verrou_4 (.e(verrou_3_s), .h(not_2_out), .S(verrou_4_s));
  Verrou verrou_5 (.e(verrou_4_s), .h(clock_1_out), .S(verrou_5_s));
  not not_3 (not_3_out, clock_1_out);
  Verrou verrou_6 (.e(verrou_5_s), .h(not_3_out), .S(S));
endmodule

module HADD (
  input  B,
  input  A,
  output S,
  output R
);

  and and_1 (R, A, B);
  xor xor_1 (S, A, B);
endmodule

module INC3 (
  input  in_1,
  input  in_2,
  input  in_3,
  output out_4,
  output out_5,
  output out_6
);

  wire hadd_1_r, hadd_2_r, hadd_3_r;

  HADD hadd_1 (.A(in_1), .B(1'b1), .R(hadd_1_r), .S(out_4));
  HADD hadd_2 (.A(in_2), .B(hadd_1_r), .R(hadd_2_r), .S(out_5));
  HADD hadd_3 (.A(in_3), .B(hadd_2_r), .R(hadd_3_r), .S(out_6));
  // also tied to GND on the sheet: hadd_3_r
endmodule

module Compteur3 (
  input  in_1,
  output out_2,
  output out_3,
  output out_4
);

  wire bacule_d_1_s, bacule_d_2_s, bacule_d_3_s, clock_1_out, inc3_1_out_4, inc3_1_out_5, inc3_1_out_6,
       not_1_out;

  Clock clock_1 (.out(clock_1_out));
  Bacule_D bacule_d_1 (.h(clock_1_out), .e(out_2), .S(bacule_d_1_s));
  Bacule_D bacule_d_2 (.h(clock_1_out), .e(out_3), .S(bacule_d_2_s));
  Bacule_D bacule_d_3 (.h(clock_1_out), .e(out_4), .S(bacule_d_3_s));
  INC3 inc3_1 (
    .in_1(bacule_d_1_s), .in_2(bacule_d_2_s), .in_3(bacule_d_3_s), .out_4(inc3_1_out_4),
    .out_5(inc3_1_out_5), .out_6(inc3_1_out_6));
  not not_1 (not_1_out, in_1);
  and and_1 (out_2, inc3_1_out_4, not_1_out);
  and and_2 (out_3, inc3_1_out_5, not_1_out);
  and and_3 (out_4, inc3_1_out_6, not_1_out);
endmodule
